# Fritzing sketch Car (saved by Fritzing 1.0.6)
perfboards: 1

parts:
  Mod1 = Raspberry Pi 4B
  HC-SR04_Sensor_1 = HC-SR04 Ultrasonic Distance Sensor
  HC-SR04_Sensor_2 = HC-SR04 Ultrasonic Distance Sensor
  HC-SR04_Sensor_3 = HC-SR04 Ultrasonic Distance Sensor
  J1 = Piezo Speaker  # not connected
  S1 = H-Bridge with L298N
  S2 = H-Bridge with L298N
  M1 = fc-51 [package=THT]
  M2 = fc-51 [package=THT]
  U3 = Header 6 [package=1x06_smd_straight_alt]
  U4 = Header 8 [package=1x08_smd]  # not connected
  U5 = Header 6 [package=1x06_smd_straight_alt]
  U6 = Header 8 [package=1x08_smd]  # not connected
  U7 = Header 8 [package=1x08_smd]
  U8 = Header 6 [package=1x06_smd_straight_alt]  # not connected
  U9 = Header 8 [package=1x08_smd]
  U10 = Header 6 [package=1x06_smd_straight_alt]  # not connected
  U11 = Header 8 [package=1x08_smd]
  U12 = Header 6 [package=1x06_smd_straight_alt]
  U13 = Header 8 [package=1x08_smd]
  U14 = Header 6 [package=1x06_smd_straight_alt]
  U15 = Header 6 [package=1x06_smd_straight_alt]  # not connected
  U16 = Header 6 [package=1x06_smd_straight_alt]  # not connected
  U17 = Header 8 [package=1x08_smd]
  U18 = Header 8 [package=1x08_smd]
  U19 = AVR 10-pin ICSP Header [package=avr_icsp]  # not connected
  U20 = AVR 10-pin ICSP Header [package=avr_icsp]  # not connected
  IC2 = IC, DIP package, 20 pins [chip_label="Altera Cyclone II EP2C5T144"]  # not connected
  Power_plug1 = Power plug  # not connected
  U21 = LIPO-1000mAh [package=lipo-1000]
  U22 = LIPO-1000mAh [package=lipo-1000]
  M5 = DC Motor [voltage_(max)=6V voltage_(min)=3V]
  M6 = DC Motor [voltage_(max)=6V voltage_(min)=3V]
  M7 = DC Motor [voltage_(max)=6V voltage_(min)=3V]
  M8 = DC Motor [voltage_(max)=6V voltage_(min)=3V]
  Q1 = TRANSISTOR_NPN [package=to-92-ammo]
  R1 = Resistor [tolerance=±5% resistance=1k package="2010 [SMD]"]
  R2 = Resistor [tolerance=±5% power=0.25W resistance=20k package=THT]
  R3 = Resistor [tolerance=±5% power=0.25W resistance=10k package=THT]
  R4 = Resistor [tolerance=±5% power=0.25W resistance=20k package=THT]
  R5 = Resistor [tolerance=±5% power=0.25W resistance=10k package=THT]
  R6 = Resistor [tolerance=±5% power=0.25W resistance=10k package=THT]
  R7 = Resistor [tolerance=±5% power=0.25W resistance=20k package=THT]
  R8 = Resistor [tolerance=±5% power=0.25W resistance=20k package=THT]
  R9 = Resistor [tolerance=±5% power=0.25W resistance=10k package=THT]
  R10 = Resistor [tolerance=±5% power=0.25W resistance=20k package=THT]
  R11 = Resistor [tolerance=±5% power=0.25W resistance=10k package=THT]

nets:
  N1: Mod1.GPIO4, U14.5
  N2: Mod1.GPIO17, U18.8
  N3: Mod1.GPIO27, U12.5
  N4: Mod1.GPIO22, U13.2
  N5: Mod1.GPIO23, U12.6
  N6: Mod1.GPIO24, U14.6
  N7: Mod1.GPIO12, U11.1
  N8: Mod1.GPIO16, U13.1
  N9: Mod1.GPIO26, U12.4
  N10: HC-SR04_Sensor_1.TRIG, U11.3
  N11: HC-SR04_Sensor_1.ECHO, R3.Pin_1
  VCC: HC-SR04_Sensor_2.VCC, HC-SR04_Sensor_3.VCC
  N12: HC-SR04_Sensor_2.TRIG, U11.4
  N13: HC-SR04_Sensor_2.ECHO, R5.Pin_1
  GND: HC-SR04_Sensor_2.GND, HC-SR04_Sensor_3.GND
  N14: HC-SR04_Sensor_3.TRIG, U11.5
  N15: HC-SR04_Sensor_3.ECHO, R6.Pin_1
  N16: S1.12V, U22.+
  N17: S1.GND, U22.-
  N18: S1.ENA, S1.ENA-5V
  N19: S1.IN1, U3.4
  N20: S1.IN2, U5.4
  N21: S1.IN3, U3.3
  N22: S1.IN4, U5.3
  N23: S1.ENB, S1.ENB-5V
  N24: S1.M1-01, M7.pin_2
  N25: S1.M1-02, M7.pin_1
  N26: S1.M2-01, M5.pin_2
  N27: S1.M2-02, M5.pin_1
  N28: S2.12V, U21.+
  N29: S2.GND, U21.-
  N30: S2.ENA, S2.ENA-5V
  N31: S2.IN1, U9.4
  N32: S2.IN2, U7.4
  N33: S2.IN3, U9.5
  N34: S2.IN4, U7.5
  N35: S2.ENB, S2.ENB-5V
  N36: S2.M1-01, M6.pin_2
  N37: S2.M1-02, M6.pin_1
  N38: S2.M2-01, M8.pin_2
  N39: S2.M2-02, M8.pin_1
  N40: M1.pin1, R11.Pin_1
  N41: M1.pin2, M2.pin2
  N42: M1.pin3, M2.pin1
  N43: M2.pin3, R9.Pin_1
  N44: U11.6, R8.Pin_1, R9.Pin_0
  N45: U13.3, R2.Pin_1, R3.Pin_0
  N46: U13.4, R4.Pin_1, R5.Pin_0
  N47: U13.5, R6.Pin_0, R7.Pin_1
  N48: U13.6, R10.Pin_1
  N49: U17.8, R1.Pin_0
  N50: Q1.B, R1.Pin_1

custom parts:
  H-Bridge with L298N: h-bridge
